# Fritzing sketch kGeigieBreadboard (saved by Fritzing 0.9.4)
breadboards: 1

parts:
  R1 = Resistor [tolerance=±5% resistance=220 package="2512 [SMD]"]  # not connected
  R2 = Resistor [tolerance=±5% resistance=220 package="2512 [SMD]"]
  C1 = Ceramic Capacitor [capacitance="100 nF" package="1206 [SMD, multilayer]"]
  R4 = Resistor [tolerance=±5% resistance=220 package="2512 [SMD]"]
  R3 = Resistor [tolerance=±5% resistance=220 package=THT]
  U1 = TRANSISTOR_NPN_2 [package=to-92]
  LED2 = LED - 3mm [color="Red (633nm)" package="3 mm [THT]"]

nets:
  N1: R2.Pin_1, C1.0, R4.Pin_0
  N2: C1.1, R3.Pin_1
  N3: R4.Pin_1, U1.E
  N4: R3.Pin_0, LED2.anode
  N5: U1.B, LED2.cathode
