# Fritzing sketch kGeigieBreadboard_rob (saved by Fritzing 0.9.6b)
circuit board: 8.46667cm x 5.64444cm
breadboards: 1

parts:
  C1 = Ceramic Capacitor [capacitance="100 nF" voltage=35V package="1206 [SMD, multilayer]"]
  U1 = TRANSISTOR_NPN_2 [package=to-92]
  LED2 = LED - 3mm [color="Red (633nm)" package="3 mm [THT]"]
  U2 = GEIGER_TUBE [package=geiger_tube]  # not connected
  D1 = Rectifier Diode [part_number=1N4001 package="Melf DO-213 AB [SMD]"]
  R5 = Resistor [tolerance=±5% resistance=56 package=THT]
  M5StickC1 = M5StickC  # not connected
  R6 = Resistor [tolerance=±5% resistance=1k package=THT]  # not connected
  R7 = Resistor [tolerance=±5% resistance=100k package=THT]
  R8 = Resistor [tolerance=±5% resistance=220 package=THT]  # not connected
  VCC1 = Battery

nets:
  N1: C1.0, U1.E, VCC1.-
  N2: C1.1, D1.cathode, R7.Pin_0
  N3: U1.C, LED2.anode
  N4: U1.B, R7.Pin_1
  N5: LED2.cathode, R5.Pin_0
  N6: R5.Pin_1, VCC1.+
